# Fritzing sketch scheme (saved by Fritzing 0.9.3b)
breadboards: 1

parts:
  V1 = DC Power [voltage=5]
  U1 = LM124-324 Quad Opamp [package="DIP (Dual Inline)"]
  U2 = LM124-324 Quad Opamp [package="DIP (Dual Inline)"]
  R1 = Resistor [tolerance=±5% resistance=220 package=THT]
  R2 = Resistor [tolerance=±5% resistance=1k package=THT]
  R3 = Resistor [tolerance=±5% resistance=220 package=THT]
  R4 = Resistor [tolerance=±5% resistance=220 package=THT]
  J1 = female pin header, 2 pins [form="♀ (female)"]
  J2 = female pin header, 2 pins [form="♀ (female)"]
  R5 = Resistor [tolerance=±5% resistance=330 package=THT]
  R6 = Resistor [tolerance=±5% resistance=330 package=THT]
  SP1 = SPEAKER [package=pcb_mount_speaker]
  Q1 = NPN-Transistor [package="TO92 [THT]"]
  C1 = Electrolytic Capacitor [capacitance=4.7mF package="100 mil [THT, electrolytic]"]
  R8 = Resistor [tolerance=±5% resistance=330 package=THT]
  R9 = Resistor [tolerance=±5% resistance=1k package=THT]
  R10 = Resistor [tolerance=±5% resistance=330 package=THT]
  R11 = Resistor [tolerance=±5% resistance=220 package=THT]
  R12 = Resistor [tolerance=±5% resistance=220 package=THT]
  R13 = Resistor [tolerance=±5% resistance=220 package=THT]
  LED1 = LED - 5mm [color="Yellow (595nm)" package="5 mm [THT]"]
  LED2 = LED - 5mm [color="Yellow (595nm)" package="5 mm [THT]"]
  LED3 = LED - 5mm [color="Yellow (595nm)" package="5 mm [THT]"]
  LED4 = LED - 5mm [color="Yellow (595nm)" package="5 mm [THT]"]
  10k = TRIMPOT [package=trimpot-3mm]
  R15 = PHOTOCELL [package=photocell]
  R16 = PHOTOCELL [package=photocell]
  R17 = PHOTOCELL [package=photocell]
  R18 = PHOTOCELL [package=photocell]
  R19 = Resistor [tolerance=±5% resistance=10k package=THT]
  R20 = Resistor [tolerance=±5% resistance=220 package=THT]
  R21 = Resistor [tolerance=±5% resistance=220 package=THT]
  R22 = Resistor [tolerance=±5% resistance=220 package=THT]
  R23 = Resistor [tolerance=±5% resistance=1 package=THT]
  R24 = Resistor [tolerance=±5% resistance=220 package=THT]
  R25 = Resistor [tolerance=±5% resistance=220 package=THT]
  R26 = Resistor [tolerance=±5% resistance=220 package=THT]
  LED5 = LED - 5mm [color="Red (633nm)" package="5 mm [THT]"]
  LED6 = LED - 5mm [color="Red (633nm)" package="5 mm [THT]"]
  LED7 = LED - 5mm [color="Red (633nm)" package="5 mm [THT]"]
  LED8 = LED - 5mm [color="Red (633nm)" package="5 mm [THT]"]
  C2 = Electrolytic Capacitor [capacitance=1µF package="100 mil [THT, electrolytic]"]
  J3 = female pin header, 2 pins [form="♀ (female)"]
  J4 = female pin header, 2 pins [form="♀ (female)"]
  Raspberry_Pi_1 = Raspberry Pi 3 [part_number=RPI-3-V1.2]
  J5 = JST-B3P-VH [part_number=JST-B3P-VH package=THT]
  J6 = JST-B3P-VH [part_number=JST-B3P-VH package=THT]
  J7 = JST-B3P-VH [part_number=JST-B3P-VH package=THT]
  J8 = JST-B3P-VH [part_number=JST-B3P-VH package=THT]
  10k_2 = TRIMPOT [package=trimpot-3mm]

nets:
  N1: V1.V+, U1.VCC+, U2.VCC+, SP1.+, C1.+, 10k.CCW, R19.Pin_0, R20.Pin_0, R21.Pin_0, R22.Pin_0, R23.Pin_1, R24.Pin_1, R25.Pin_1, R26.Pin_1, C2.+, Raspberry_Pi_1.5V
  N2: V1.V-, U1.VCC-, U2.VCC-, R5.Pin_1, C1.-, R9.Pin_1, LED1.cathode, LED2.cathode, LED3.cathode, LED4.cathode, 10k.CW, R15.P$2, R16.P$2, R17.P$2, R18.P$2, LED5.cathode, LED6.cathode, LED7.cathode, LED8.cathode, C2.-, Raspberry_Pi_1.GND
  N3: U1.1OUT, R10.Pin_0
  N4: U1.1IN-, U1.2IN-, U1.3IN-, U1.4IN-, 10k.WIPER
  N5: U1.1IN+, R15.P$1, R19.Pin_1
  N6: U1.2IN+, R18.P$1, R22.Pin_1
  N7: U1.2OUT, R13.Pin_0
  N8: U1.3OUT, R12.Pin_0
  N9: U1.3IN+, R17.P$1, R21.Pin_1
  N10: U1.4IN+, R16.P$1, R20.Pin_1
  N11: U1.4OUT, R11.Pin_0
  N12: U2.3OUT, R8.Pin_0, 10k_2.WIPER, 10k_2.CW
  N13: U2.3IN-, R9.Pin_0, 10k_2.CCW
  N14: U2.3IN+, U2.4OUT, R6.Pin_0
  N15: U2.4IN+, R1.Pin_0, R2.Pin_0, R3.Pin_0, R4.Pin_0
  N16: U2.4IN-, R5.Pin_0, R6.Pin_1
  N17: R1.Pin_1, J2.pin1
  N18: R2.Pin_1, J2.pin2
  N19: R3.Pin_1, J1.pin2
  N20: R4.Pin_1, J1.pin1
  N21: SP1.-, Q1.C
  GND: Q1.E
  N22: Q1.B, R8.Pin_1
  N23: R10.Pin_1, LED1.anode, J3.pin1
  N24: R11.Pin_1, LED2.anode, J3.pin2
  N25: R12.Pin_1, LED3.anode, J4.pin1
  N26: R13.Pin_1, LED4.anode, J4.pin2
  N27: R23.Pin_0, LED5.anode
  N28: R24.Pin_0, LED6.anode
  N29: R25.Pin_0, LED7.anode
  N30: R26.Pin_0, LED8.anode
  N31: Raspberry_Pi_1.GPIO27, J5.pin2
  N32: Raspberry_Pi_1.GPIO22, J5.pin1
  N33: Raspberry_Pi_1.GPIO5, J8.pin3
  N34: Raspberry_Pi_1.GPIO6, J8.pin2
  N35: Raspberry_Pi_1.GPIO13, J7.pin3
  N36: Raspberry_Pi_1.GPIO12, J8.pin1
  N37: Raspberry_Pi_1.GPIO23, J6.pin3
  N38: Raspberry_Pi_1.GPIO18, J5.pin3

notes:
  Arpa laser, Black is ground. White is +5v.
