# Fritzing sketch circuit (saved by Fritzing 0.9.3b)
breadboards: 1

parts:
  VR1 = Voltage Regulator [package=to-220-alt]
  VR2 = Voltage Regulator [package=to-220-alt]
  V1 = DC Power [voltage=12V]
  D2 = Diode [package=diode-hv]
  D3 = Diode [package=diode-hv]
  R1 = Resistor [tolerance=±5% resistance=4.7k package="2512 [SMD]"]
  D4 = Diode [package=diode-hv]
  C5 = Ceramic Capacitor [capacitance=10µF voltage=35V package="200 mil [THT, multilayer]"]
  C6 = Ceramic Capacitor [capacitance=10µF voltage=35V package="200 mil [THT, multilayer]"]
  IC3 = Voltage Regulator LM1117 [package=sot223]
  R4 = TRIMPOT [package=trim_pot_pth]
  U1 = OPA344 [package=sot23-5]
  T1 = LM35 Temperature Sensor [package="TO92 [THT]"]
  U2 = OPA344 [package=sot23-5]
  R6 = Resistor [tolerance=±5% resistance=10k package=THT]
  LED1 = LEDs [package=led10mm]
  U4 = OPA344 [package=sot23-5]
  U5 = OPA344 [package=sot23-5]
  U6 = OPA344 [package=sot23-5]
  R9 = Resistor [tolerance=±5% resistance=10k package=THT]
  R10 = Resistor [tolerance=±5% resistance=10k package=THT]
  C8 = Ceramic Capacitor [capacitance=10µF package="100 mil [THT, multilayer]"]
  R11 = Resistor [tolerance=±5% resistance=100k package=THT]
  R12 = Resistor [tolerance=±5% resistance=100k package=THT]
  C9 = Ceramic Capacitor [capacitance=10µF package="100 mil [THT, multilayer]"]
  U7 = OPA344 [package=sot23-5]
  TIP122 = NPN-Transistor [package="TO92 [THT]"]
  R13 = Resistor [tolerance=±5% resistance=10k package=THT]
  R15 = Resistor [tolerance=±5% resistance=1k package=THT]
  R16 = Resistor [tolerance=±5% resistance=7.05k package=THT]
  R17 = Resistor [tolerance=±5% resistance=100k package=THT]
  R18 = Resistor [tolerance=±5% resistance=27 package=THT]
  U8 = OPA344 [package=sot23-5]
  R19 = Resistor [tolerance=±5% resistance=1M package=THT]
  U3 = OPA344 [package=sot23-5]
  R20 = Resistor [tolerance=±5% resistance=10k package=THT]
  R21 = Resistor [tolerance=±5% resistance=10k package=THT]
  R22 = Resistor [tolerance=±5% resistance=10k package=THT]
  D5 = Diode [package=diode-hv]
  R14 = Resistor [tolerance=±5% resistance=100 package=THT]

nets:
  GND: VR1.GND, VR2.GND, D4.A
  N1: VR1.IN, VR2.IN, V1.V+, TIP122.C
  N2: VR1.OUT, D3.A, C5.1
  N3: VR2.OUT, D2.A, C6.1
  GND_2: V1.V-, R1.Pin_0, D4.C, C5.0, C6.0, IC3.ADJ, R4.CW, T1.GND, U4.+IN, U5.+IN, U6.+IN, U7.+IN, R17.Pin_0, R18.Pin_1, R19.Pin_1, R22.Pin_1
  N4: D2.C, D3.C, IC3.IN, T1.+Vs, LED1.A
  N5: R1.Pin_1, LED1.C
  N6: IC3.OUT, R4.CCW
  N7: R4.WIPER, U1.+IN
  N8: U1.OUT, U1.-IN, R20.Pin_0
  N9: T1.Vout, U2.+IN, R17.Pin_1
  N10: U2.OUT, U2.-IN, R6.Pin_0
  N11: R6.Pin_1, U3.-IN, R21.Pin_0
  N12: U4.OUT, R10.Pin_0, R14.Pin_1
  N13: U4.-IN, R9.Pin_0, R10.Pin_1
  N14: U5.OUT, R12.Pin_0, R15.Pin_1
  N15: U5.-IN, C8.0, R12.Pin_1
  N16: U6.OUT, C9.0, R16.Pin_1
  N17: U6.-IN, R11.Pin_0, C9.1
  N18: R9.Pin_1, C8.1, R11.Pin_1, U3.OUT, R21.Pin_1
  N19: U7.OUT, R13.Pin_0, D5.A
  N20: U7.-IN, R13.Pin_1, R15.Pin_0, R16.Pin_0, R14.Pin_0
  N21: TIP122.E, R18.Pin_0, U8.-IN
  N22: TIP122.B, U8.OUT
  N23: U8.+IN, R19.Pin_0, D5.C
  N24: U3.+IN, R20.Pin_1, R22.Pin_0
