# Fritzing sketch circuit (saved by Fritzing 0.9.3b)
breadboards: 1

parts:
  VR1 = Voltage Regulator [package=to-220-alt]
  VR2 = Voltage Regulator [package=to-220-alt]
  V1 = DC Power [voltage=12V]
  D2 = Diode [package=diode-hv]
  D3 = Diode [package=diode-hv]
  R1 = Resistor [tolerance=±5% resistance=4.7k package="2512 [SMD]"]
  D4 = Diode [package=diode-hv]
  C5 = Ceramic Capacitor [capacitance=10µF voltage=35V package="200 mil [THT, multilayer]"]
  C6 = Ceramic Capacitor [capacitance=10µF voltage=35V package="200 mil [THT, multilayer]"]
  IC3 = Voltage Regulator LM1117 [package=sot223]
  C7 = Ceramic Capacitor [capacitance=10µF voltage=35V package="200 mil [THT, multilayer]"]
  R2 = Resistor [tolerance=±5% resistance=220 package=THT]
  R3 = Resistor [tolerance=±5% resistance=220 package=THT]
  R4 = TRIMPOT [package=trim_pot_pth]
  U1 = OPA344 [package=sot23-5]
  T1 = LM35 Temperature Sensor [package="TO92 [THT]"]
  R5 = Resistor [tolerance=±5% resistance=220 package=THT]
  U2 = OPA344 [package=sot23-5]
  R6 = Resistor [tolerance=±5% resistance=220 package=THT]
  LED1 = LEDs [package=led10mm]
  R7 = Resistor [tolerance=±5% resistance=220 package=THT]
  R8 = Resistor [tolerance=±5% resistance=220 package=THT]
  U3 = OPA344 [package=sot23-5]
  U4 = OPA344 [package=sot23-5]
  U5 = OPA344 [package=sot23-5]
  R9 = Resistor [tolerance=±5% resistance=220 package=THT]
  R10 = Resistor [tolerance=±5% resistance=220 package=THT]
  C8 = Ceramic Capacitor [capacitance=100nF package="100 mil [THT, multilayer]"]
  R11 = Resistor [tolerance=±5% resistance=220 package=THT]
  R12 = Resistor [tolerance=±5% resistance=220 package=THT]
  C9 = Ceramic Capacitor [capacitance=100nF package="100 mil [THT, multilayer]"]
  U6 = OPA344 [package=sot23-5]
  TIP122 = NPN-Transistor [package="TO92 [THT]"]
  Peltier = Peltier Element
  R13 = Resistor [tolerance=±5% resistance=220 package=THT]
  R14 = Resistor [tolerance=±5% resistance=220 package=THT]
  R15 = Resistor [tolerance=±5% resistance=220 package=THT]
  R16 = Resistor [tolerance=±5% resistance=220 package=THT]
  R17 = Resistor [tolerance=±5% resistance=220 package=THT]

nets:
  GND: VR1.GND, VR2.GND, D4.A
  N1: VR1.IN, VR2.IN, V1.V+, TIP122.C
  N2: VR1.OUT, D3.A, C5.1
  N3: VR2.OUT, D2.A, C6.1
  GND_2: V1.V-, R1.Pin_0, D4.C, C5.0, C6.0, IC3.ADJ, C7.0, R3.Pin_1, R4.CW, R8.Pin_1
  N4: D2.C, D3.C, IC3.IN, T1.+Vs, LED1.A
  N5: R1.Pin_1, LED1.C
  N6: IC3.OUT, C7.1, R2.Pin_0
  N7: R2.Pin_1, R3.Pin_0, U1.+IN
  N8: R4.CCW, U1.OUT, U1.-IN
  N9: R4.WIPER, R7.Pin_0
  N10: T1.Vout, R5.Pin_0, R17.Pin_1
  N11: T1.GND, U3.+IN, U4.+IN, U5.+IN, U6.+IN, Peltier.pin2, R17.Pin_0
  N12: R5.Pin_1, U2.-IN, R6.Pin_0
  N13: U2.OUT, R6.Pin_1, R9.Pin_1, C8.1, R11.Pin_1
  N14: U2.+IN, R7.Pin_1, R8.Pin_0
  N15: U3.OUT, R10.Pin_0, R14.Pin_1
  N16: U3.-IN, R9.Pin_0, R10.Pin_1
  N17: U4.OUT, R12.Pin_0, R15.Pin_1
  N18: U4.-IN, C8.0, R12.Pin_1
  N19: U5.OUT, C9.0, R16.Pin_1
  N20: U5.-IN, R11.Pin_0, C9.1
  N21: U6.OUT, TIP122.B, R13.Pin_0
  N22: U6.-IN, R13.Pin_1, R14.Pin_0, R15.Pin_0, R16.Pin_0
  N23: TIP122.E, Peltier.pin1
