# Fritzing sketch Sketch (saved by Fritzing 0.9.3b)
breadboards: 1

parts:
  T1 = LM35 Temperature Sensor [package="TO92 [THT]"]
  Part1 = Adafruit ADS1115 16Bit I2C ADC [part_number="Adafruit #1085"]
  Raspberry_Pi_1 = Raspberry Pi 3 [part_number=RPI-3-V1.2]
  J3 = Screw terminal - 2 pins [package=THT]
  J4 = Screw terminal - 2 pins [package=THT]
  IC1 = Voltage Regulator [package=78xxl]
  LED1 = LED - 3mm [color="Yellow (585nm)" package="3 mm [THT]"]
  R2 = Resistor [tolerance=±5% resistance=4.7k package=THT]
  D1 = Rectifier Diode [part_number=1N4001 package="300 mil [THT]"]
  D2 = Rectifier Diode [part_number=1N4001 package="300 mil [THT]"]
  C2 = Electrolytic Capacitor [capacitance=1µF voltage=10V package="100 mil [THT, electrolytic]"]
  C2_2 = Electrolytic Capacitor [capacitance=4.7µF voltage=10V package="100 mil [THT, electrolytic]"]
  C1 = Electrolytic Capacitor [capacitance=4.7mF package="100 mil [THT, electrolytic]"]
  IC2 = Voltage Regulator [package=78xxl]
  D3 = Rectifier Diode [part_number=1N4001 package="300 mil [THT]"]
  C3 = Electrolytic Capacitor [capacitance=4.7µF voltage=16V package="100 mil [THT, electrolytic]"]
  R3 = Resistor [tolerance=±5% resistance=4.7k package=THT]
  LED2 = LED - 3mm [color="Red (635nm)" package="3 mm [THT]"]
  R1 = Resistor [tolerance=±5% resistance=3.3k package=THT]
  R1_2 = Resistor [tolerance=±5% resistance=3.3k package=THT]
  R1_3 = Resistor [tolerance=±5% resistance=68k package="2512 [SMD]"]
  R1_4 = Resistor [tolerance=±5% resistance=82k package=THT]
  R1_5 = Resistor [tolerance=±5% resistance=82k package=THT]

nets:
  3V3: T1.+Vs, Part1.VDD, Raspberry_Pi_1.3v3, Raspberry_Pi_1.3V3
  N1: T1.Vout, Part1.AIN0, R1.Pin_0, R1_2.Pin_0, R1_3.Pin_0, R1_4.Pin_0, R1_5.Pin_0
  GND: T1.GND, Part1.GND, Raspberry_Pi_1.GND, R1.Pin_1, R1_2.Pin_1, R1_3.Pin_1, R1_4.Pin_1, R1_5.Pin_1
  N2: Part1.SDA, Raspberry_Pi_1.GPIO2
  N3: Part1.SCL, Raspberry_Pi_1.GPIO3
  N4: J3.pin1, J4.pin2, LED1.cathode, D1.cathode, C2.-, C2_2.-, C1.-, C3.-, LED2.cathode
  N5: J3.pin2, IC1.IN, R2.Pin_1, C1.+, IC2.IN
  GND_2: IC1.GND, D1.anode, IC2.GND
  N6: IC1.OUT, D2.anode, C2.+, C2_2.+
  N7: LED1.anode, R2.Pin_0
  N8: D2.cathode, D3.cathode, R3.Pin_0
  N9: IC2.OUT, D3.anode, C3.+
  N10: R3.Pin_1, LED2.anode

custom parts:
  Adafruit ADS1115 16Bit I2C ADC: For microcontrollers without an analog-to-digital converter or when you want a higher-precision ADC, the ADS1115 provides 16-bit precision at 860 samples/second over I2C. The chip can be configured as 4 single-ended input channels, or two differential channels. As a nice bonus, it even includes a programmable gain amplifier, up to x16, to help boost up smaller single/differential signals to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
